// Logisim project Four_Bits_Add_Sub.circ as structural Verilog: 2 circuits, main circuit Add_Sub_4Bits
module Add_Sub_4Bits (
  input  [3:0] A,
  input  [3:0] B,
  input  Add_Sub,
  output Overflow,
  output [3:0] R,
  output Zero
);

  wire add_1bit_1_cout, add_1bit_2_cout, add_1bit_3_cout, add_1bit_4_cout, not_2_out, or_1_out, xor_2_out,
       xor_3_out, xor_4_out, xor_5_out;

  xor xor_1 (Overflow, add_1bit_1_cout, add_1bit_2_cout);
  // Probe on R
  // Probe on A
  Add_1Bit add_1bit_1 (.Sum(R[3]), .A(A[3]), .B(xor_2_out), .Cout(add_1bit_1_cout), .Cin(add_1bit_2_cout));
  xor xor_2 (xor_2_out, not_2_out, B[3]);
  Add_1Bit add_1bit_2 (.Sum(R[2]), .A(A[2]), .B(xor_3_out), .Cout(add_1bit_2_cout), .Cin(add_1bit_3_cout));
  xor xor_3 (xor_3_out, not_2_out, B[2]);
  Add_1Bit add_1bit_3 (.Sum(R[1]), .A(A[1]), .B(xor_4_out), .Cout(add_1bit_3_cout), .Cin(add_1bit_4_cout));
  not not_1 (Zero, or_1_out);
  or or_1 (or_1_out, R[0], R[1], R[2], R[3]);
  // Probe on B
  xor xor_4 (xor_4_out, not_2_out, B[1]);
  Add_1Bit add_1bit_4 (.Sum(R[0]), .A(A[0]), .B(xor_5_out), .Cout(add_1bit_4_cout), .Cin(not_2_out));
  xor xor_5 (xor_5_out, not_2_out, B[0]);
  not not_2 (not_2_out, Add_Sub);

  // Notes on the sheet:
  //   Byungwoo Kim, ID 260621422
  //   MAKE SURE THAT YOU OPENED THIS PROJECT IN "LOGISIM-EVOLUTION"
  //   YOU CAN FIND "LOGISIM-EVOLUTION" PROGRAM IN THE ASSIGNMENT'S FOLDER
  //   DO NOT USE "LOGISIM" VERSION TO SOLVE THIS ASSIGNMENT!
endmodule

module Add_1Bit (
  input  A,
  input  B,
  input  Cin,
  output Sum,
  output Cout
);

  wire and_1_out, and_2_out, xor_1_out;

  xor xor_1 (xor_1_out, A, B);
  xor xor_2 (Sum, xor_1_out, Cin);
  and and_1 (and_1_out, xor_1_out, Cin);
  and and_2 (and_2_out, A, B);
  or or_1 (Cout, and_1_out, and_2_out);

  // Notes on the sheet:
  //   Byungwoo Kim, ID 260621422
  //   MAKE SURE THAT YOU OPENED THIS PROJECT IN "LOGISIM-EVOLUTION"
  //   YOU CAN FIND "LOGISIM-EVOLUTION" PROGRAM IN THE ASSIGNMENT'S FOLDER
  //   DO NOT USE "LOGISIM" VERSION TO SOLVE THIS ASSIGNMENT!
endmodule
